# Fritzing sketch 1-Wire Arduino (saved by Fritzing 0.9.6b)
breadboards: 1

parts:
  Part1 = Arduino Uno (Rev3) - ICSP
  U1 = 712-52 1-Wire Mifare Classic RFID Reader [part_number=712-52 package="SIP (Single Inline) [THT]"]
  R1 = Resistor [tolerance=±5% power=0.25 resistance=4.7k package=THT]
  J1 = Piezo Speaker

nets:
  N1: Part1.GND, U1.Power_(-), J1.pin1
  N2: Part1.D8, U1.LED_(Green)
  N3: Part1.D10_PWM/SS, U1.1-Wire, R1.Pin_1
  N4: Part1.D3_PWM, J1.pin2
  N5: Part1.D7, U1.LED_(Red)
  N6: Part1.5V, R1.Pin_0
  N7: Part1.VIN, U1.Power_(+)

custom parts:
  712-52 1-Wire Mifare Classic RFID Reader: A Mifare Classic RFID reader, with 1-Wire data output and 2 built in LEDs, Green and Red
